# Fritzing sketch PicoDMG_diagrama (saved by Fritzing 0.9.5d)
perfboards: 1

parts:
  SD1 = micro SD module (SPI, 3V3) [package=THT]
  AMP1 = MAX98357A I2S Amp [part_number=MAX98357A package=THT]
  U1 = Waveshare Core2350B [part_number=Core2350B package=THT]
  J1 = Jack P2 3.5mm SMD 5 pinos [part_number="3.5 5p" package=SMD]
  R1 = Resistor [tolerance=±5% resistance=100 package="0603 [SMD]"]
  J2 = FPC-10P 0.5mm adapter [package=THT]
  R2 = Resistor [tolerance=±5% resistance=1k package="0603 [SMD]"]
  BAT1 = Battery Holders [part_number=103450 package=lipo-1100mAh]
  J3 = USB-C 4 pinos PTH adapter [part_number="USB-C x DIP" package=THT]
  U2 = TP4056 USB-C com protecao [part_number=TP4056 package=THT]
  J4 = Piezo Speaker [part_number="SPK GB 1W"]
  R3 = Resistor [tolerance=±5% resistance=100k package="0603 [SMD]"]
  R4 = Resistor [tolerance=±5% resistance=100k package="0603 [SMD]"]
  R5 = Resistor [tolerance=±5% resistance=100k package="0603 [SMD]"]
  R6 = Resistor [tolerance=±5% resistance=100k package="0603 [SMD]"]
  C1 = Capacitor [part_number=100nf package=cap-pth-small2]
  U3 = Vibration Motor- ROB-08449 [part_number="Rumble 1034" package=vibe-motor-10mm]
  D1 = Rectifier Diode [part_number=1N4007 package="300 mil [THT]"]
  R7 = Resistor [tolerance=±5% resistance=1k package="0603 [SMD]"]
  Q3 = NPN-Transistor [part_number=BC337 package="TO92 [THT]"]
  Q4 = NPN-Transistor [part_number=BC337 package="TO92 [THT]"]
  JP1 = Header 12 [package=1x12_machine-pin-header_lock.004]
  JP2 = Header 1 [package=1x01_offset]
  S1 = SPST Switch [part_number=On/Off package=switch-spdt_kit]

nets:
  3V3: SD1.3V3, AMP1.Vin, U1.3V3, J2.2, J2.6, J2.7, U3.-, D1.cathode
  N1: SD1.CS, U1.GP13
  N2: SD1.MOSI, U1.GP15
  N3: SD1.CLK, U1.GP14
  N4: SD1.MISO, U1.GP12
  GND: SD1.GND, AMP1.GND, U1.GND, J2.1, J3.GND, U2.OUT-, U2.IN-, R3.Pin_1, Q3.E, Q4.E, JP2.1, S1.P
  N5: AMP1.LRC, U1.GP28
  N6: AMP1.BCLK, U1.GP27
  N7: AMP1.DIN, U1.GP26
  N8: AMP1.SPK-, R1.Pin_0, J4.pin1
  N9: AMP1.SPK+, J1.TIP, J1.RING
  N10: U1.GP2, JP1.12
  N11: U1.GP4, JP1.9
  N12: U1.GP3, JP1.11
  N13: U1.GP6, JP1.8
  N14: U1.GP5, JP1.10
  N15: U1.GP8, JP1.5
  N16: U1.GP7, JP1.7
  N17: U1.GP10, S1.O
  N18: U1.GP9, JP1.6
  N19: U1.USB_DM, J3.D-
  N20: U1.USB_DP, J3.D+
  N21: U1.VBUS, BAT1.+, U2.OUT+, U2.B+, R6.Pin_1
  N22: U1.GP17, J2.5
  N23: U1.GP19, J2.3
  N24: U1.GP18, J2.4
  N25: U1.GP20, J2.10
  N26: U1.GP23, R7.Pin_0
  N27: U1.GP22, R2.Pin_0
  N28: U1.GP40, R5.Pin_0, R6.Pin_0, C1.1
  N29: U1.GP39, R3.Pin_0, R4.Pin_0
  N30: J1.SLEEVE, R1.Pin_1
  N31: J1.TIP_SW, J4.pin2
  N32: J2.8, Q4.C
  N33: R2.Pin_1, Q4.B
  N34: BAT1.-, U2.B-, R5.Pin_1, C1.2
  N35: J3.VBUS, U2.IN+, R4.Pin_1
  N36: U3.+, D1.anode, Q3.C
  N37: R7.Pin_1, Q3.B

notes:
  up
  down
  left
  right
  A
  B
  X
  Y
  L
  R
  start
  select
  <-- Display  ST7789 10P
  GND

custom parts:
  micro SD module (SPI, 3V3): Modulo leitor de cartao micro SD por SPI, 3,3 V sem regulador. Placa azul de 18,5 x 17,5 mm com 6 furos a 2,54 mm (3V3, CS, MOSI, CLK, MISO, GND). Dimensoes aproximadas, para ilustracao.
  MAX98357A I2S Amp: Modulo amplificador classe D I2S MAX98357A (3 W em 4 ohm a 5 V), placa roxa de 17,7 x 19,1 mm com header de 7 pinos a 2,54 mm e borne para o alto-falante. Dimensoes aproximadas, para ilustracao.
  Waveshare Core2350B: Waveshare Core2350B (RP2350B, 16 MB flash, PSRAM opcional 0/2/8 MB). Placa 25,4 x 25,4 mm, 64 pinos em grade 2,54 mm (anel duplo de 10x10, headers P1..P4 8x2 do esquematico oficial). USB via conector FPC 6 pinos e adaptador RP-Tiny-Adapter-B.
  Jack P2 3.5mm SMD 5 pinos: Jack P2 (3,5 mm) estereo SMD de 5 pinos, corpo 12 x 6 x 4,4 mm com bocal de 5 mm, pads numerados de 2 a 6 conforme o desenho do fabricante, 2 pinos de posicionamento de 0,9 mm. 2 = ponta (com chave NF no 6), 5 = anel, 3 = manga (com chave NA no 4).
  FPC-10P 0.5mm adapter: Adaptador de cabo FPC/FFC de 10 vias, passo 0,5 mm, para header 2 x 5 de 2,54 mm. Placa de 20 x 26 mm. O pino N do header e o contato N do FPC. Dimensoes aproximadas, para ilustracao.
  USB-C 4 pinos PTH adapter: Adaptador USB-C femea para 4 furos PTH a 2,54 mm (V, D-, D+, G). Placa de 12 x 13,8 mm. Dimensoes aproximadas, para ilustracao.
  TP4056 USB-C com protecao: Modulo carregador de bateria de litio TP4056 (1 A) com protecao DW01 + 8205A e entrada USB-C. Placa de 15 x 20 mm. B+ e OUT+ sao o mesmo no; IN- e OUT- sao o GND da placa; B- vai so na celula. Posicoes aproximadas, para ilustracao.
